// Logisim project main.circ as structural Verilog: 5 circuits, main circuit main
module main (
  input  a1,
  input  a2,
  input  Carry_in,
  input  a3,
  input  a4,
  input  b1,
  input  b2,
  input  b3,
  input  b4,
  output out_10,
  output out_11,
  output out_12,
  output out_13,
  output Overflow,
  output Carry_out
);

  wire decoder_1_a, decoder_1_b, decoder_1_c, decoder_1_d, decoder_1_e, decoder_1_f, decoder_1_g,
       decoder_2_a, decoder_2_b, decoder_2_c, decoder_2_d, decoder_2_e, decoder_2_f, decoder_2_g,
       decoder_3_a, decoder_3_b, decoder_3_c, decoder_3_d, decoder_3_e, decoder_3_f, decoder_3_g;

  decoder decoder_1 (
    .bit1(a1), .bit2(a2), .bit3(a3), .bit4(a4), .a(decoder_1_a), .b(decoder_1_b), .c(decoder_1_c),
    .d(decoder_1_d), .e(decoder_1_e), .f(decoder_1_f), .g(decoder_1_g));
  _4_bits_summer u_4_bits_summer_1 (
    .in_2(a1), .in_3(a2), .in_4(a3), .in_5(a4), .in_6(b1), .in_7(b2), .in_8(b3), .in_9(b4),
    .Carry_in(Carry_in), .Carry_out(Carry_out), .out_10(out_13), .out_11(out_12), .out_12(out_11),
    .out_13(out_10), .Overflow(Overflow));
  decoder decoder_2 (
    .bit1(b1), .bit2(b2), .bit3(b3), .bit4(b4), .a(decoder_2_a), .b(decoder_2_b), .c(decoder_2_c),
    .d(decoder_2_d), .e(decoder_2_e), .f(decoder_2_f), .g(decoder_2_g));
  _7_Segment_Display u_7_segment_display_1 (
    .g(decoder_1_a), .f(decoder_1_b), .a(decoder_1_c), .b(decoder_1_d), .e(decoder_1_e), .d(decoder_1_f),
    .c(decoder_1_g));  // open: dp
  _7_Segment_Display u_7_segment_display_2 (
    .g(decoder_2_a), .f(decoder_2_b), .a(decoder_2_c), .b(decoder_2_d), .e(decoder_2_e), .d(decoder_2_f),
    .c(decoder_2_g));  // open: dp
  decoder decoder_3 (
    .bit1(out_13), .bit2(out_12), .bit3(out_11), .bit4(out_10), .a(decoder_3_a), .b(decoder_3_b),
    .c(decoder_3_c), .d(decoder_3_d), .e(decoder_3_e), .f(decoder_3_f), .g(decoder_3_g));
  _7_Segment_Display u_7_segment_display_3 (
    .g(decoder_3_a), .f(decoder_3_b), .a(decoder_3_c), .b(decoder_3_d), .e(decoder_3_e), .d(decoder_3_f),
    .c(decoder_3_g));  // open: dp
endmodule

module half_summer (
  input  in_1,
  input  in_2,
  output sum,
  output carry_out
);

  xor xor_1 (sum, in_1, in_2);
  and and_1 (carry_out, in_1, in_2);
endmodule

module full_summer (
  input  in_1,
  input  in_2,
  input  in_3,
  output sum,
  output carry_out
);

  wire half_summer_1_carry_out, half_summer_1_sum, half_summer_2_carry_out;

  half_summer half_summer_1 (.in_1(in_2), .in_2(in_3), .sum(half_summer_1_sum), .carry_out(half_summer_1_carry_out));
  half_summer half_summer_2 (.in_1(half_summer_1_sum), .in_2(in_1), .sum(sum), .carry_out(half_summer_2_carry_out));
  or or_1 (carry_out, half_summer_1_carry_out, half_summer_2_carry_out);
endmodule

module _4_bits_summer (
  input  Carry_in,
  input  in_2,
  input  in_3,
  input  in_4,
  input  in_5,
  input  in_6,
  input  in_7,
  input  in_8,
  input  in_9,
  output out_10,
  output out_11,
  output out_12,
  output out_13,
  output Overflow,
  output Carry_out
);

  wire full_summer_1_carry_out, full_summer_2_carry_out, full_summer_3_carry_out;

  full_summer full_summer_1 (
    .in_2(in_2), .in_3(in_6), .in_1(Carry_in), .carry_out(full_summer_1_carry_out), .sum(out_10));
  full_summer full_summer_2 (
    .in_2(in_3), .in_3(in_7), .in_1(full_summer_1_carry_out), .carry_out(full_summer_2_carry_out),
    .sum(out_11));
  full_summer full_summer_3 (
    .in_2(in_4), .in_3(in_8), .in_1(full_summer_2_carry_out), .carry_out(full_summer_3_carry_out),
    .sum(out_12));
  full_summer full_summer_4 (
    .in_2(in_5), .in_3(in_9), .in_1(full_summer_3_carry_out), .carry_out(Carry_out), .sum(out_13));
  xor xor_1 (Overflow, full_summer_3_carry_out, Carry_out);
endmodule

module decoder (
  input  bit1,
  input  bit2,
  input  bit3,
  input  bit4,
  output a,
  output b,
  output c,
  output d,
  output e,
  output f,
  output g
);

  wire and_1_out, and_2_out, and_3_out, and_4_out, and_5_out, and_6_out, and_7_out, and_8_out, and_9_out,
       and_10_out, and_11_out, and_12_out, and_13_out, and_14_out, and_15_out, and_16_out, and_17_out,
       and_18_out, and_19_out, and_20_out, and_21_out, and_22_out, and_23_out, and_24_out, and_25_out,
       and_26_out, and_27_out, and_28_out, and_29_out, and_30_out, and_31_out, and_32_out, and_33_out,
       and_34_out, and_35_out, and_36_out, not_1_out, not_2_out, not_3_out, not_4_out, not_5_out, not_6_out,
       not_7_out, not_8_out, not_9_out, not_10_out, not_11_out, not_12_out, not_13_out, not_14_out,
       not_15_out, not_16_out, not_17_out, not_18_out, not_19_out, not_20_out, not_21_out, not_22_out,
       not_23_out, not_24_out, not_25_out, not_26_out, not_27_out, not_28_out, not_29_out, not_30_out,
       not_31_out, not_32_out, not_33_out, not_34_out, not_35_out, not_36_out, not_37_out, not_38_out,
       not_39_out, not_40_out, not_41_out, not_42_out, not_43_out, not_44_out, not_45_out;

  not not_1 (not_1_out, bit2);
  and and_1 (and_1_out, not_1_out, bit3);
  and and_2 (and_2_out, bit3, not_2_out);
  not not_2 (not_2_out, bit4);
  not not_3 (not_3_out, bit1);
  and and_3 (and_3_out, not_3_out, bit2, not_4_out);
  not not_4 (not_4_out, bit3);
  and and_4 (and_4_out, bit1, not_5_out);
  not not_5 (not_5_out, bit2);
  and and_5 (and_5_out, bit1, bit4);
  not not_6 (not_6_out, bit3);
  and and_6 (and_6_out, not_6_out, not_7_out);
  not not_7 (not_7_out, bit4);
  not not_8 (not_8_out, bit1);
  and and_7 (and_7_out, not_8_out, bit2, not_9_out);
  not not_9 (not_9_out, bit3);
  and and_8 (and_8_out, bit2, not_10_out);
  not not_10 (not_10_out, bit4);
  and and_9 (and_9_out, bit1, not_11_out);
  not not_11 (not_11_out, bit2);
  and and_10 (and_10_out, bit1, bit3);
  not not_12 (not_12_out, bit2);
  and and_11 (and_11_out, not_12_out, not_13_out);
  not not_13 (not_13_out, bit4);
  not not_14 (not_14_out, bit1);
  and and_12 (and_12_out, not_14_out, bit3);
  not not_15 (not_15_out, bit1);
  and and_13 (and_13_out, not_15_out, bit2, bit4);
  and and_14 (and_14_out, bit2, bit3);
  not not_16 (not_16_out, bit2);
  and and_15 (and_15_out, bit1, not_16_out, not_17_out);
  not not_17 (not_17_out, bit3);
  and and_16 (and_16_out, bit1, not_18_out);
  not not_18 (not_18_out, bit4);
  not not_19 (not_19_out, bit1);
  and and_17 (and_17_out, not_19_out, not_20_out);
  not not_20 (not_20_out, bit2);
  not not_21 (not_21_out, bit1);
  and and_18 (and_18_out, not_21_out, not_22_out, not_23_out);
  not not_22 (not_22_out, bit3);
  not not_23 (not_23_out, bit4);
  not not_24 (not_24_out, bit2);
  and and_19 (and_19_out, not_24_out, not_25_out);
  not not_25 (not_25_out, bit3);
  not not_26 (not_26_out, bit2);
  and and_20 (and_20_out, not_26_out, not_27_out);
  not not_27 (not_27_out, bit4);
  not not_28 (not_28_out, bit1);
  and and_21 (and_21_out, not_28_out, bit3, bit4);
  and and_22 (and_22_out, bit1, not_29_out, bit4);
  not not_29 (not_29_out, bit3);
  not not_30 (not_30_out, bit2);
  and and_23 (and_23_out, not_30_out, not_31_out);
  not not_31 (not_31_out, bit4);
  and and_24 (and_24_out, bit3, not_32_out);
  not not_32 (not_32_out, bit4);
  and and_25 (and_25_out, bit1, bit3);
  and and_26 (and_26_out, bit1, bit2);
  not not_33 (not_33_out, bit1);
  and and_27 (and_27_out, not_33_out, not_34_out, not_35_out);
  not not_34 (not_34_out, bit2);
  not not_35 (not_35_out, bit4);
  not not_36 (not_36_out, bit2);
  and and_28 (and_28_out, not_36_out, bit3, bit4);
  not not_37 (not_37_out, bit3);
  and and_29 (and_29_out, bit2, not_37_out, bit4);
  and and_30 (and_30_out, bit2, bit3, not_38_out);
  not not_38 (not_38_out, bit4);
  and and_31 (and_31_out, bit1, not_39_out);
  not not_39 (not_39_out, bit3);
  not not_40 (not_40_out, bit1);
  and and_32 (and_32_out, not_40_out, not_41_out);
  not not_41 (not_41_out, bit3);
  not not_42 (not_42_out, bit1);
  and and_33 (and_33_out, not_42_out, bit4);
  not not_43 (not_43_out, bit3);
  and and_34 (and_34_out, not_43_out, bit4);
  not not_44 (not_44_out, bit1);
  and and_35 (and_35_out, not_44_out, bit2);
  and and_36 (and_36_out, bit1, not_45_out);
  not not_45 (not_45_out, bit2);
  or or_1 (a, and_1_out, and_2_out, and_3_out, and_4_out, and_5_out);
  or or_2 (b, and_6_out, and_7_out, and_8_out, and_9_out, and_10_out);
  or or_3 (e, and_23_out, and_24_out, and_25_out, and_26_out);
  or or_4 (f, and_27_out, and_28_out, and_29_out, and_30_out, and_31_out);
  or or_5 (g, and_32_out, and_33_out, and_34_out, and_35_out, and_36_out);
  or or_6 (c, and_11_out, and_12_out, and_13_out, and_14_out, and_15_out, and_16_out);
  or or_7 (d, and_17_out, and_18_out, and_19_out, and_20_out, and_21_out, and_22_out);
endmodule
