// Logisim project outro.circ as structural Verilog: 3 circuits, main circuit main
module main (
  input  [3:0] in_1,
  input  [3:0] in_2,
  input  [3:0] in_3,
  output [3:0] out_4
);

  ula_completa ula_completa_1 (.A(in_2), .B(in_3), .Op(in_1), .out_4(out_4));
endmodule

module mini_ula_4bits (
  input  a,
  input  [3:0] in_2,
  input  b,
  output S
);

  wire and_1_out, and_2_out, and_3_out, nand_1_out, not_1_out, not_2_out, not_3_out, not_4_out, not_5_out,
       not_6_out, or_1_out, or_2_out, or_3_out, xor_1_out;

  not not_1 (not_1_out, a);
  not not_2 (not_2_out, a);
  and and_1 (and_1_out, not_2_out, b);
  nor nor_1 (not_1_out, a, b);
  not not_3 (not_3_out, b);
  nand nand_1 (nand_1_out, a, b);
  not not_4 (not_4_out, b);
  and and_2 (and_2_out, a, not_4_out);
  xor xor_1 (xor_1_out, a, b);
  not not_5 (not_5_out, a);
  or or_1 (or_1_out, not_5_out, b);
  xnor xnor_1 (or_1_out, a, b);
  and and_3 (and_3_out, a, b);
  not not_6 (not_6_out, b);
  or or_2 (or_2_out, a, not_6_out);
  or or_3 (or_3_out, a, b);
  Multiplexer #(.select(4), .enable("false")) multiplexer_1 (
    .in0(not_1_out), .in1(not_1_out), .in2(and_1_out), .in3(1'b0), .in4(nand_1_out), .in5(not_3_out),
    .in6(xor_1_out), .in7(and_2_out), .in8(or_1_out), .in9(or_1_out), .in10(b), .in11(and_3_out),
    .in12(1'b1), .in13(or_2_out), .in14(or_3_out), .in15(a), .out(S), .sel(in_2));
endmodule

module ula_completa (
  input  [3:0] A,
  input  [3:0] B,
  input  [3:0] Op,
  output [3:0] out_4
);

  mini_ula_4bits mini_ula_4bits_1 (.a(B[0]), .b(A[0]), .in_2(Op), .S(out_4[0]));
  mini_ula_4bits mini_ula_4bits_2 (.a(B[1]), .b(A[1]), .in_2(Op), .S(out_4[1]));
  mini_ula_4bits mini_ula_4bits_3 (.a(B[2]), .b(A[2]), .in_2(Op), .S(out_4[2]));
  mini_ula_4bits mini_ula_4bits_4 (.a(B[3]), .b(A[3]), .in_2(Op), .S(out_4[3]));
endmodule
