// Logisim project main.circ as structural Verilog: 3 circuits, main circuit main
module main (
  input  [3:0] in_1,
  input  [3:0] in_2,
  input  in_3,
  input  [1:0] in_4,
  output [3:0] out_5,
  output out_6
);

  ula_4_bits ula_4_bits_1 (.A(in_1), .B(in_2), .BinInvert(in_3), .Op(in_4), .out_6(out_6), .S(out_5));
endmodule

module mini_ula (
  input  BinInverter,
  input  Carry_in,
  input  [1:0] Operations,
  input  A,
  input  B,
  output Result,
  output Carry_Out
);

  wire adder_1_out, and_1_out, multiplexer_1_out, not_1_out, not_2_out, or_1_out;

  not not_1 (not_1_out, B);
  Multiplexer #(.enable("false")) multiplexer_1 (.in0(B), .in1(not_1_out), .out(multiplexer_1_out), .sel(BinInverter));
  and and_1 (and_1_out, A, multiplexer_1_out);
  or or_1 (or_1_out, A, multiplexer_1_out);
  not not_2 (not_2_out, A);
  Adder #(.width(1)) adder_1 (.a(A), .b(multiplexer_1_out), .out(adder_1_out), .cin(Carry_in), .cout(Carry_Out));
  Multiplexer #(.select(2), .enable("false")) multiplexer_2 (
    .in0(and_1_out), .in1(or_1_out), .in2(not_2_out), .in3(adder_1_out), .out(Result), .sel(Operations));
endmodule

module ula_4_bits (
  input  [3:0] A,
  input  [3:0] B,
  input  BinInvert,
  input  [1:0] Op,
  output [3:0] S,
  output out_6
);

  wire mini_ula_1_carry_out, mini_ula_2_carry_out, mini_ula_3_carry_out;

  mini_ula mini_ula_1 (
    .A(B[0]), .B(A[0]), .BinInverter(BinInvert), .Carry_in(BinInvert), .Operations(Op),
    .Carry_Out(mini_ula_1_carry_out), .Result(S[0]));
  mini_ula mini_ula_2 (
    .A(B[1]), .B(A[1]), .BinInverter(BinInvert), .Carry_in(mini_ula_1_carry_out), .Operations(Op),
    .Carry_Out(mini_ula_2_carry_out), .Result(S[1]));
  mini_ula mini_ula_3 (
    .A(B[2]), .B(A[2]), .BinInverter(BinInvert), .Carry_in(mini_ula_2_carry_out), .Operations(Op),
    .Carry_Out(mini_ula_3_carry_out), .Result(S[2]));
  mini_ula mini_ula_4 (
    .A(B[3]), .B(A[3]), .BinInverter(BinInvert), .Carry_in(mini_ula_3_carry_out), .Operations(Op),
    .Carry_Out(out_6), .Result(S[3]));
endmodule
